# Fritzing sketch climanode-wiring (saved by Fritzing 1.0.8)
breadboards: 1

parts:
  esp1 = ESP32 DevKitc V4
  LCD1 = LCD screen
  U1 = TRANSISTOR_NPN_2 [package=to-92]
  R1 = Resistor [tolerance=±5% resistance=220 package="0402 [SMD]"]
  R2 = TRIMPOT [maximum_resistance=10kΩ knob_status=50% power=0.5W package=trim_pot_pth]
  DHT1 = DHT22 Humidity and Temperature Sensor
  RE1 = KY-040 Rotary encoder [package=THT]
  GY-NEO6MV1 = GY-NEO6MV2

nets:
  N1: esp1.IO15, LCD1.DB7
  N2: esp1.IO4, RE1.DT
  N3: esp1.IO16, LCD1.DB6
  N4: esp1.IO17, LCD1.DB5
  N5: esp1.IO18, LCD1.DB4
  N6: esp1.IO19, LCD1.RS
  N7: esp1.IO21, DHT1.DATA
  N8: esp1.IO22, RE1.CLK
  N9: esp1.IO23, LCD1.E
  GND: esp1.GND, LCD1.VSS, LCD1.R/W, U1.E, R2.CW, DHT1.GND, RE1.GND, GY-NEO6MV1.GND
  N10: esp1.IO34, GY-NEO6MV1.Tx
  N11: esp1.IO26, R1.Pin_0
  N12: esp1.IO27, RE1.SW
  N13: esp1.IO13, GY-NEO6MV1.Rx
  VDD: esp1.5V, LCD1.VDD, LCD1.LED+, R2.CCW, DHT1.VDD, RE1.Vcc, GY-NEO6MV1.Vcc
  N14: LCD1.V0, R2.WIPER
  N15: LCD1.LED-, U1.C
  N16: U1.B, R1.Pin_1

custom parts:
  ESP32 DevKitc V4: ESP32-DevKitC board with ESP32-WROOM-32 module. ESP32-DevKitC V4 is a small-sized ESP32-based development board produced by Espressif. Most of the pins on the ESP module are broken out to the pin headers on the board. The pins D0, D1, D2, D3, CMD and CLK are used internally for communication between ESP32 and SPI flash memory. They are grouped on both sides near the USB connector. Avoid using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
  KY-040 Rotary encoder: KY-040 Rotary Encoder with switch on breakout borad from AZ Delivery
  GY-NEO6MV2: Description: Module GPS , type GY-NEO6MV2, pour arduino et autres micro-contrôleurs. Caractéristiques De type GY-NEO6MV2 Alimentation 3V-5V Avec Flight Control EEPROM MWC Antenne large céramique, fort signal, 25 x 25 mm Paramètres de configuration sauvegardés en EEPROM Avec batterie de backup de données LED témoin de signal Module miniaturisé 25 x 35 mm Trou de fixation de 3mm Baud rate par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
